# Fritzing sketch DynamixelShield (saved by Fritzing 0.7.7b)

parts:
  Part1 = Arduino ProtoShield
  IC1 = IC, DIP package, 8 pins [chip_label=MAX485 part_number=MAX485CPA+]
  R1 = Resistor [tolerance=±5% resistance=10k package=THT]
  C1 = Ceramic Capacitor [capacitance=10µF package="100 mil [THT, multilayer]"]
  12VDC = Power plug
  Dynamixel_Connector_(Pin_1_ground) = female pin header, 4 pins [form="♀ (female)"]

nets:
  N1: Part1.5V, Part1.N$68, IC1.pin4, R1.Pin_0, C1.0
  GND: Part1.GND, Part1.N$5, Part1.N$101, IC1.pin1, C1.1, 12VDC.GND, Dynamixel_Connector_(Pin_1_ground).pin1
  VIN: Part1.VIN, Part1.N$10, 12VDC.VCC, Dynamixel_Connector_(Pin_1_ground).pin2
  N2: Part1.RX, Part1.N$71, IC1.pin5, R1.Pin_1
  N3: Part1.TX, Part1.N$104, IC1.pin8
  N4: Part1.D2, Part1.N$82, Part1.N$93, IC1.pin6, IC1.pin7
  N5: Part1.N$11, Part1.N$90, IC1.pin2, Dynamixel_Connector_(Pin_1_ground).pin3
  N6: Part1.N$12, Part1.N$79, IC1.pin3, Dynamixel_Connector_(Pin_1_ground).pin4

notes:
  Not yet implemented.
